# Fritzing sketch kasokudo_sensa_LED_hikaruyatu (saved by Fritzing 0.9.2b)
breadboards: 1

parts:
  パーツ1 = Arduino Uno (Rev3)
  U2 = ADXL345 [package=lga14]

nets:
  GND: パーツ1.A4/SDA, パーツ1.A5/SCL, パーツ1.GND, U2.GND, U2.NC, U2.SCL
  3V3: パーツ1.3V3, U2.VDD, U2.CS
